# Fritzing sketch balance (saved by Fritzing 0.9.3b)
breadboards: 1

parts:
  U1 = atmega328 [package=dip]
  Nokia_5110_LCD_Module1 = Nokia 5110 LCD
  Composant1 = Adafruit FTDI Friend [part_number="Adafruit #284"]
  Composant2 = HX711 Weighing Sensor Module
  TP1 = TP4056 [chip_label=TP4056 package="DIP (Dual Inline) [THT]"]
  U2 = LIPO-2000mAh [package=lipo-2000]
  XTAL1 = Crystal [frequency="16 Mhz" package=SMD]
  C1 = Capacitor [package=cap-pth-small2]
  C2 = Capacitor [package=cap-pth-small2]
  C3 = Ceramic Capacitor [capacitance=100nF package="100 mil [THT, multilayer]"]
  R1 = Resistor [tolerance=±5% resistance=1k package="0402 [SMD]"]
  S5 = Pushbutton [package="[SMD]"]
  S6 = Pushbutton [package="[SMD]"]
  S7 = Pushbutton [package="[SMD]"]
  R2 = Resistor [tolerance=±5% resistance=10k package="0805 [SMD]"]
  R3 = Resistor [tolerance=±5% resistance=10k package="0805 [SMD]"]
  S2 = Load Sensor - 50kg [part_number=SEN-10245]
  S4 = Load Sensor - 50kg [part_number=SEN-10245]
  S1 = Load Sensor - 50kg [part_number=SEN-10245]
  S3 = Load Sensor - 50kg [part_number=SEN-10245]

nets:
  N1: U1.RESET, C3.0, R1.Pin_1, S7.Pin_1, S7.Pin_2
  N2: U1.D0_(RX), Composant1.TX
  N3: U1.D1_(TX), Composant1.RX
  N4: U1.D2, S6.Pin_3, S6.Pin_4, R3.Pin_1
  N5: U1.D3_(PWM), S5.Pin_3, S5.Pin_4, R2.Pin_1
  N6: U1.D4, Nokia_5110_LCD_Module1.GND
  VCC: U1.VCC, U1.AVCC, Nokia_5110_LCD_Module1.DN(MOSI), Composant1.VCC, Composant2.VCC, TP1.pin3, R1.Pin_0, S5.Pin_1, S5.Pin_2, S6.Pin_1, S6.Pin_2
  GND: U1.GND, Nokia_5110_LCD_Module1.LED, Composant1.GND, Composant2.GND, TP1.pin6, C1.2, C2.1, S7.Pin_3, S7.Pin_4, R2.Pin_0, R3.Pin_0
  N7: U1.XLAT1, XTAL1.pin_0, C2.2
  N8: U1.XLAT2, XTAL1.pin_1, C1.1
  N9: U1.D5_(PWM), Nokia_5110_LCD_Module1.SCE
  N10: U1.D6_(PWM), Nokia_5110_LCD_Module1.VCC
  N11: U1.D7, Nokia_5110_LCD_Module1.SCLK
  N12: U1.D11_(PWM), Nokia_5110_LCD_Module1.RST
  N13: U1.D13, Nokia_5110_LCD_Module1.D/C
  N14: U1.A2, Composant2.DO/RX
  N15: U1.A3, Composant2.CK/TX
  N16: Composant1.RTS/DTR, C3.1
  N17: Composant2.E+, S2.R
  N18: Composant2.E-, S4.R
  N19: Composant2.A+, S1.R
  N20: Composant2.A-, S3.R
  N21: TP1.pin4, U2.+
  N22: TP1.pin5, U2.-
  N23: S2.B, S3.B
  N24: S2.W, S1.W
  N25: S4.B, S1.B
  N26: S4.W, S3.W

notes:
  chargeur USB
  entrée programmation
  Balance 0 à 200kg

custom parts:
  Nokia 5110 LCD: Nokia 5110 Graphic 84*48 LCD module such as the Sparkfun LCD-10168 or the clones from Ebay. There is example code for the Arduino available from the Sparkfun site in https://learn.sparkfun.com/tutorials/graphic-lcd-hookup-guide This is a 3.3V device, if you are running it from a 5V micro you need a 5V tolorant level translator such as the 74ahc367 to protect the signal imputs. Rafa G. did a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
  Adafruit FTDI Friend: Long gone are the days of parallel ports and serial ports. Now the USB port reigns supreme! But USB is hard, and you just want to transfer your every-day serial data from a microcontroller to computer. What now? Enter the FTDI Friend! The FTDI Friend is a tweaked out FTDI FT232RL chip adapter. Sure, like the well-known FTDI cable, it can provide power to your project and there are 4 signal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
  HX711 Weighing Sensor Module: HX711 is a precision 24-bit analog-to-digital converter (ADC) designed for weigh scales and industrial control applications to interface directly with a bridge sensor.
  TP4056: A DIP stand-in part for whatever IC you want. With 6 pins on a 300mil dual inline package (DIP) footprint.
  Load Sensor - 50kg: Half-wheatstone bridge Load Cell modified from the Fritzing Repo This load sensor, sometimes called a strain gauge, is the same one found in digital bathroom scales (you know, the ones you use in January for your New Year's resolutions, and then forget about a month later). This sensor can measure up to about 110 pounds.
